# Fritzing sketch BluetoothWeatherStation_V2 (saved by Fritzing 0.9.3b)
circuit board: 4.70334cm x 5.50996cm
breadboards: 1

parts:
  R1 = Resistor [tolerance=±5% resistance=100 package=THT]
  R2 = Resistor [tolerance=±5% resistance=220 package=THT]
  S1 = Toggle Switch [package=THT]
  BMP180/BME280 = Barometric Pressure Sensor - BMP180 Breakout (GY-68)
  Serial_Dev = Header 3 [package=screwterminal-3.5mm-3_lock.007s]
  VCC1 = Battery
  Tensy_2_0 = PJRC Tensy 2.0
  R3 = Resistor [tolerance=±5% resistance=4.7k package=THT]
  R4 = Resistor [tolerance=±5% resistance=2.2k package=THT]
  LED1 = LED - 5mm [color="Red (633nm)" part_number="low voltage warning" package="5 mm [THT]"]
  HC_05 = Bluetooth HC-05 Macho [part_number="Hc 05"]

nets:
  N1: R1.Pin_0, R2.Pin_1, BMP180/BME280.VCC
  N2: R1.Pin_1, S1.L1, Serial_Dev.1, VCC1.+, R3.Pin_0, HC_05.VCC
  GND: R2.Pin_0, S1.L2, BMP180/BME280.GND, Serial_Dev.3, VCC1.-, Tensy_2_0.D10, R4.Pin_1, LED1.cathode, HC_05.GND
  N3: S1.COM, Tensy_2_0.D9
  N4: BMP180/BME280.SCL, Tensy_2_0.A2
  N5: BMP180/BME280.SDA, Tensy_2_0.A3
  N6: Serial_Dev.2, Tensy_2_0.RAW
  N7: Tensy_2_0.VCC, HC_05.TXD
  N8: Tensy_2_0.RESET, HC_05.RXD
  N9: Tensy_2_0.SCK, R3.Pin_1, R4.Pin_0
  N10: Tensy_2_0.MISO, LED1.anode

notes:
  Bluetooth Weather Sensor V1.0.4. B. Fritz 2020. CC BY-NC-SA 2.5
  Low voltage
  TX
  RX
  Serial Input
  SDA
  SCL
  Vltg low
  Vltg low out
  100
  220
  4,7 k
  2,2 k
  +

custom parts:
  PJRC Tensy 2.0: approach to Arduino. This is a 5V Arduino running the 16MHz bootloader. Arduino Pro Mini does not come with connectors populated so that you can solder in any connector or wire with any orientation you need. We recommend first time Arduino users start with the Uno R3. It's a great board that will get you up and running quickly. The Arduino Pro series is meant for users that understand the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
